# Fritzing sketch esp32_sndchip_ym2149 (saved by Fritzing 0.9.4)
circuit board: 8.46667cm x 5.64444cm
breadboards: 1

parts:
  U1 = NodeMCU V1.0
  IC1 = IC, DIP package, 40 pins [chip_label=YM2149]
  U2 = LM386 [package=dip08]  # not connected
  C1 = Ceramic Capacitor [capacitance=100nF package="100 mil [THT, multilayer]"]
  TRS1 = Audio Jack (TRS) 3.5mm [package="4Ucon 08780 [THT]"]  # not connected

nets:
  N1: U1.GND, IC1.pin1, C1.1
  N2: U1.Vin, IC1.pin40, C1.0

custom parts:
  NodeMCU V1.0: ESP8266 based NodeMCU
